# Fritzing sketch circuit_v1 (saved by Fritzing 0.9.3b)
breadboards: 1

parts:
  ESP32_DevBoard = LuaNode32 / ESP32
  Part1 = Motor Driver 1A Dual TB6612FNG
  M1 = DC Motor
  Potentiometer = Rotary Potentiometer (Small) [maximum_resistance=100kΩ package=THT]

nets:
  N1: ESP32_DevBoard.D13, Potentiometer.wiper
  GND: ESP32_DevBoard.GND, Part1.GND, Potentiometer.leg1
  5V: ESP32_DevBoard.Vin, Part1.VM
  3.3V: ESP32_DevBoard.3V3, Part1.VCC, Part1.STBY, Potentiometer.leg2
  A01: ESP32_DevBoard.D18, Part1.AIN1
  A02: ESP32_DevBoard.D19, Part1.AIN2
  EnA: ESP32_DevBoard.D21, Part1.PWMA
  N2: Part1.A02, M1.pin_2
  N3: Part1.A01, M1.pin_1

notes:
  PID Test Kit, 1

custom parts:
  LuaNode32 / ESP32: ESP32 based LuaNode32
